// Logisim project PRESENT.circ as structural Verilog
module S_box (
  input  in_1,
  input  in_2,
  input  in_3,
  input  in_4
);

  wire y0_1_out_5, y1_1_out_5, y2_1_out_5, y3_1_out_5;

  y0 y0_1 (.in_1(in_2), .in_2(in_3), .in_3(in_4), .in_4(in_1), .out_5(y0_1_out_5));
  y1 y1_1 (.in_1(in_2), .in_2(in_3), .in_3(in_4), .in_4(in_1), .out_5(y1_1_out_5));
  y2 y2_1 (.in_1(in_2), .in_2(in_3), .in_3(in_4), .in_4(in_1), .out_5(y2_1_out_5));
  y3 y3_1 (.in_1(in_2), .in_2(in_3), .in_3(in_4), .in_4(in_1), .out_5(y3_1_out_5));
  DotMatrix #(.matrixcols(4), .matrixrows(1)) dotmatrix_1 (
    .col0(y3_1_out_5), .col1(y2_1_out_5), .col2(y1_1_out_5), .col3(y0_1_out_5));
endmodule

module y0 (
  input  in_1,
  input  in_2,
  input  in_3,
  input  in_4,
  output out_5
);

  wire and_1_out, and_2_out, and_3_out, and_4_out, and_5_out, and_6_out, not_1_out, not_2_out, not_3_out,
       not_4_out;

  not not_1 (not_1_out, in_1);
  not not_2 (not_2_out, in_2);
  not not_3 (not_3_out, in_3);
  not not_4 (not_4_out, in_4);
  and and_1 (and_1_out, not_1_out, in_2, not_3_out, not_4_out);
  and and_2 (and_2_out, in_1, not_2_out, not_4_out);
  and and_3 (and_3_out, in_1, in_3, not_4_out);
  and and_4 (and_4_out, not_1_out, not_2_out, in_4);
  and and_5 (and_5_out, not_1_out, in_3, in_4);
  and and_6 (and_6_out, in_1, in_2, in_4, not_3_out);
  or or_1 (out_5, and_1_out, and_2_out, and_3_out, and_4_out, and_5_out, and_6_out);
endmodule

module y1 (
  input  in_1,
  input  in_2,
  input  in_3,
  input  in_4,
  output out_5
);

  wire and_1_out, and_2_out, and_3_out, and_4_out, and_5_out, not_1_out, not_2_out, not_3_out, not_4_out;

  not not_1 (not_1_out, in_1);
  not not_2 (not_2_out, in_2);
  not not_3 (not_3_out, in_3);
  not not_4 (not_4_out, in_4);
  and and_1 (and_1_out, in_1, not_2_out, not_4_out);
  and and_2 (and_2_out, in_1, not_3_out, in_4);
  and and_3 (and_3_out, in_1, in_2, in_4);
  and and_4 (and_4_out, not_1_out, not_2_out, in_3);
  and and_5 (and_5_out, not_1_out, in_3, not_4_out);
  or or_1 (out_5, and_1_out, and_2_out, and_3_out, and_4_out, and_5_out);
endmodule

module y2 (
  input  in_1,
  input  in_2,
  input  in_3,
  input  in_4,
  output out_5
);

  wire and_1_out, and_2_out, and_3_out, and_4_out, and_5_out, not_1_out, not_2_out, not_3_out, not_4_out;

  not not_1 (not_1_out, in_1);
  not not_2 (not_2_out, in_2);
  not not_3 (not_3_out, in_3);
  not not_4 (not_4_out, in_4);
  and and_1 (and_1_out, not_1_out, not_2_out, not_3_out);
  and and_2 (and_2_out, not_2_out, in_3, not_4_out);
  and and_3 (and_3_out, in_1, in_2, not_3_out);
  and and_4 (and_4_out, in_1, not_3_out, in_4);
  and and_5 (and_5_out, not_1_out, in_2, in_3, in_4);
  or or_1 (out_5, and_1_out, and_2_out, and_3_out, and_4_out, and_5_out);
endmodule

module y3 (
  input  in_1,
  input  in_2,
  input  in_3,
  input  in_4,
  output out_5
);

  wire and_1_out, and_2_out, and_3_out, and_4_out, and_5_out, not_1_out, not_2_out, not_3_out, not_4_out;

  not not_1 (not_1_out, in_1);
  not not_2 (not_2_out, in_2);
  not not_3 (not_3_out, in_3);
  not not_4 (not_4_out, in_4);
  and and_1 (and_1_out, not_1_out, not_3_out, not_4_out);
  and and_2 (and_2_out, not_1_out, in_3, in_4);
  and and_3 (and_3_out, not_1_out, in_2, in_3);
  and and_4 (and_4_out, in_1, not_2_out, in_4);
  and and_5 (and_5_out, in_1, not_2_out, in_3);
  or or_1 (out_5, and_1_out, and_2_out, and_3_out, and_4_out, and_5_out);
endmodule
